// Logisim project cpu.circ as structural Verilog: 6 circuits, main circuit cpu
module cpu (
);

  wire CLK, RST;
  wire [4:0] multiplexer_2_out, multiplexer_3_out, multiplexer_4_out;
  wire [15:0] \总周期数 , \无条件分支指令数 , \有条件分支成功跳转 , \有条件分支指令数 ;
  wire [23:0] divider1_1_out_2, divider_1_out_2;
  wire [31:0] alu_1_result, mips_ram_1_p4, multiplexer_1_out, multiplexer_5_out, multiplexer_6_out,
       npc_1_out_2, PC_q, registerfile_1_p6, registerfile_1_p7, rom_1_data, SyscallOut;

  Button \u_总复位  (.out(RST));
  NPC npc_1 (.in_1(PC_q), .out_2(npc_1_out_2));
  Clock clock_1 (.out(CLK));
  Divider divider_1 (.in_1(PC_q), .out_2(divider_1_out_2));
  Register #(.width(32)) PC (.D(npc_1_out_2), .Q(PC_q), .clk(CLK));  // open: en, clr
  Hex_Digit_Display hex_digit_display_1 (.value(SyscallOut[27:24]));  // open: dp
  Hex_Digit_Display hex_digit_display_2 (.value(SyscallOut[31:28]));  // open: dp
  Hex_Digit_Display hex_digit_display_3 (.value(SyscallOut[19:16]));  // open: dp
  Hex_Digit_Display hex_digit_display_4 (.value(SyscallOut[23:20]));  // open: dp
  Hex_Digit_Display hex_digit_display_5 (.value(SyscallOut[11:8]));  // open: dp
  Hex_Digit_Display hex_digit_display_6 (.value(SyscallOut[15:12]));  // open: dp
  Decoder decoder_1 (.in_1(rom_1_data));  // open: out_2, out_3, out_4, out_5, out_6, out_7, out_8, out_9
  ROM #(.addrWidth(24), .dataWidth(32)) rom_1 (.addr(divider_1_out_2), .data(rom_1_data));  // open: sel
  Hex_Digit_Display hex_digit_display_7 (.value(SyscallOut[7:4]));  // open: dp
  Hex_Digit_Display hex_digit_display_8 (.value(SyscallOut[3:0]));  // open: dp
  Multiplexer #(.select(2), .width(32), .disabled(0), .enable("false")) multiplexer_1 (
    .in3(mips_ram_1_p4), .out(multiplexer_1_out));  // open: in0, in1, in2, sel
  Multiplexer #(.select(2), .width(5), .disabled(0), .enable("false")) multiplexer_2 (.out(multiplexer_2_out));  // open: in0, in1, in2, in3, sel
  Multiplexer #(.width(5), .disabled(0), .enable("false")) multiplexer_3 (.out(multiplexer_3_out));  // open: in0, in1, sel
  Multiplexer #(.width(5), .disabled(0), .enable("false")) multiplexer_4 (.out(multiplexer_4_out));  // open: in0, in1, sel
  // Probe on \总周期数 
  // Probe on \无条件分支指令数 
  // Probe on \有条件分支指令数 
  // Probe on \有条件分支成功跳转 
  // RegisterFile registerfile_1: pin names not known; wires that end beside it: multiplexer_1_out, CLK, multiplexer_2_out, multiplexer_3_out, multiplexer_4_out, registerfile_1_p6, registerfile_1_p7
  Multiplexer #(.width(32), .disabled(0), .enable("false")) multiplexer_5 (
    .in0(registerfile_1_p6), .out(multiplexer_5_out));  // open: in1, sel
  ALU alu_1 (
    .X(multiplexer_5_out), .Result(alu_1_result), .Y(multiplexer_6_out));  // open: AluOP, Equal, Signed_Overflow, Result_2, UnSigned_Overflow
  Multiplexer #(.select(2), .width(32), .disabled(0), .enable("false")) multiplexer_6 (
    .in3(registerfile_1_p7), .out(multiplexer_6_out));  // open: in0, in1, in2, sel
  Divider1 divider1_1 (.in_1(alu_1_result), .out_2(divider1_1_out_2));
  // MIPS_RAM mips_ram_1: pin names not known; wires that end beside it: divider1_1_out_2, registerfile_1_p7, CLK, mips_ram_1_p4

  // Notes on the sheet:
  //   数码管输出应该用寄存器锁存，否则显示数据只能一闪而过
  //   可以通过项目增加Logisim库的方式将前几次实验完成的电路作为子电路引入到本电路中使用
  //   数码管输出
  //   总复位信号应将除ROM以外所有存储组件全部清零
endmodule

module Controller (
  input  [31:0] in_1
);


  // Other names for the same wires on the sheet: Instruction[31:0] = in_1
endmodule

module NPC (
  input  [31:0] in_1,
  output [31:0] out_2
);

  Adder #(.width(32)) adder_1 (.a(in_1), .b(32'h4), .out(out_2));  // open: cin, cout

  // Other names for the same wires on the sheet: Input[31:0] = in_1; Output[31:0] = out_2
endmodule

module Divider (
  input  [31:0] in_1,
  output [23:0] out_2
);


  assign out_2 = in_1[25:2];

  // Other names for the same wires on the sheet: Input[31:0] = in_1; Output[23:0] = in_1[25:2]
endmodule

module Divider1 (
  input  [31:0] in_1,
  output [23:0] out_2
);


  assign out_2 = in_1[23:0];

  // Other names for the same wires on the sheet: Input[31:0] = in_1; Output[23:0] = in_1[23:0]
endmodule

module Decoder (
  input  [31:0] in_1,
  output [4:0] out_2,
  output [5:0] out_3,
  output [4:0] out_4,
  output [25:0] out_5,
  output [4:0] out_6,
  output [5:0] out_7,
  output [4:0] out_8,
  output [15:0] out_9
);


  assign out_2 = in_1[10:6];
  assign out_3 = in_1[31:26];
  assign out_4 = in_1[25:21];
  assign out_5 = in_1[25:0];
  assign out_6 = in_1[20:16];
  assign out_7 = in_1[5:0];
  assign out_8 = in_1[15:11];
  assign out_9 = in_1[15:0];

  // Other names for the same wires on the sheet: funct[5:0] = in_1[5:0]; IMM[15:0] = in_1[15:0]; Input[31:0] = in_1;
  //   label[25:0] = in_1[25:0]; s[4:0] = in_1[10:6]; rd[4:0] = in_1[15:11]; rt[4:0] = in_1[20:16];
  //   rs[4:0] = in_1[25:21]; op[5:0] = in_1[31:26]
endmodule
